// Logisim project ALU.circ as structural Verilog: 14 circuits, main circuit main
module main (
  input  [15:0] in_1,
  input  [15:0] in_2,
  input  [5:0] in_3,
  output [15:0] out_4,
  output out_5,
  output out_6
);

  ALU alu_1 (.X(in_1), .Y(in_2), .ControlBits(in_3), .O(out_4), .ng(out_5), .zr(out_6));
endmodule

module Set0 (
  input  [15:0] in_1,
  output [15:0] out_2
);

  and and_1 (out_2[0], in_1[0], 1'b0);

  assign out_2[15:1] = {15{1'b0}};
endmodule

module Set1 (
  input  [15:0] in_1,
  output [15:0] out_2
);

  or or_1 (out_2[0], in_1[0], 1'b1);

  assign out_2[15:1] = {15{1'b1}};
endmodule

module BitAdder2 (
  input  A0,
  input  A1,
  input  B0,
  input  B1,
  output s0,
  output s1,
  output carry
);

  wire and_1_out, and_2_out, and_3_out, and_5_out, and_7_out, not_1_out, not_2_out, not_3_out, not_4_out,
       or_1_out, or_2_out, or_3_out, or_4_out;

  or or_1 (or_1_out, A1, B1);
  and and_1 (and_1_out, A1, B1);
  or or_2 (or_2_out, A0, B0);
  and and_2 (and_2_out, A0, B0);
  not not_1 (not_1_out, and_1_out);
  not not_2 (not_2_out, and_2_out);
  or or_3 (or_3_out, and_2_out, and_7_out);
  and and_3 (and_3_out, and_2_out, and_7_out);
  not not_3 (not_3_out, and_3_out);
  and and_4 (s0, or_1_out, not_1_out);
  and and_5 (and_5_out, or_2_out, not_2_out);
  and and_6 (carry, or_3_out, not_3_out);
  and and_7 (and_7_out, and_5_out, and_1_out);
  or or_4 (or_4_out, and_5_out, and_1_out);
  not not_4 (not_4_out, and_7_out);
  and and_8 (s1, or_4_out, not_4_out);
endmodule

module BitAdder4 (
  input  [3:0] A,
  input  [3:0] B,
  output [3:0] Carry,
  output [3:0] S
);

  wire bitadder2_1_carry, bitadder2_1_s0, bitadder2_1_s1, bitadder2_2_carry, bitadder2_3_carry;

  BitAdder2 bitadder2_1 (
    .A0(A[3]), .A1(A[2]), .B0(B[3]), .B1(B[2]), .s0(bitadder2_1_s0), .s1(bitadder2_1_s1),
    .carry(bitadder2_1_carry));
  BitAdder2 bitadder2_2 (.A0(A[1]), .A1(A[0]), .B0(B[1]), .B1(B[0]), .s0(S[0]), .s1(S[1]), .carry(bitadder2_2_carry));
  BitAdder2 bitadder2_3 (
    .A0(bitadder2_1_s1), .A1(bitadder2_1_s0), .B0(1'b0), .B1(bitadder2_2_carry), .s0(S[2]), .s1(S[3]),
    .carry(bitadder2_3_carry));
  BitAdder2 bitadder2_4 (
    .A0(1'b0), .A1(bitadder2_1_carry), .B0(1'b0), .B1(bitadder2_3_carry), .s0(Carry[0]), .s1(Carry[1]),
    .carry(Carry[2]));

  assign Carry[3] = 1'b0;
endmodule

module BitAdder8 (
  input  [7:0] A,
  input  [7:0] B,
  output [7:0] S,
  output [7:0] Carry
);

  wire [3:0] bitadder4_1_carry, bitadder4_1_s, bitadder4_2_carry, bitadder4_3_carry;

  BitAdder4 bitadder4_1 (.A(B[7:4]), .B(A[7:4]), .Carry(bitadder4_1_carry), .S(bitadder4_1_s));
  BitAdder4 bitadder4_2 (.A(B[3:0]), .B(A[3:0]), .Carry(bitadder4_2_carry), .S(S[3:0]));
  BitAdder4 bitadder4_3 (.A(bitadder4_1_s), .B(bitadder4_2_carry), .Carry(bitadder4_3_carry), .S(S[7:4]));
  BitAdder4 bitadder4_4 (.A(bitadder4_3_carry), .B(bitadder4_1_carry), .Carry(Carry[7:4]), .S(Carry[3:0]));
endmodule

module BitAdder16 (
  input  [15:0] A,
  input  [15:0] B,
  output [15:0] S
);

  wire [7:0] bitadder8_1_carry, bitadder8_2_carry, bitadder8_2_s, bitadder8_3_carry;

  BitAdder8 bitadder8_1 (.A(A[7:0]), .B(B[7:0]), .S(S[7:0]), .Carry(bitadder8_1_carry));
  BitAdder8 bitadder8_2 (.A(A[15:8]), .B(B[15:8]), .S(bitadder8_2_s), .Carry(bitadder8_2_carry));
  BitAdder8 bitadder8_3 (.A(bitadder8_1_carry), .B(bitadder8_2_s), .S(S[15:8]), .Carry(bitadder8_3_carry));
endmodule

module Not16Bit (
  input  [15:0] in_1,
  output [15:0] out_2
);

  not not_1 (out_2[0], in_1[0]);
  not not_2 (out_2[1], in_1[1]);
  not not_3 (out_2[2], in_1[2]);
  not not_4 (out_2[3], in_1[3]);
  not not_5 (out_2[4], in_1[4]);
  not not_6 (out_2[5], in_1[5]);
  not not_7 (out_2[6], in_1[6]);
  not not_8 (out_2[7], in_1[7]);
  not not_9 (out_2[8], in_1[8]);
  not not_10 (out_2[9], in_1[9]);
  not not_11 (out_2[10], in_1[10]);
  not not_12 (out_2[11], in_1[11]);
  not not_13 (out_2[12], in_1[12]);
  not not_14 (out_2[13], in_1[13]);
  not not_15 (out_2[14], in_1[14]);
  not not_16 (out_2[15], in_1[15]);
endmodule

module And16BIt (
  input  [15:0] in_1,
  input  [15:0] in_2,
  output [15:0] out_3
);

  and and_1 (out_3[0], in_1[0], in_2[0]);
  and and_2 (out_3[1], in_2[1], in_1[1]);
  and and_3 (out_3[2], in_2[2], in_1[2]);
  and and_4 (out_3[3], in_2[3], in_1[3]);
  and and_5 (out_3[4], in_2[4], in_1[4]);
  and and_6 (out_3[5], in_2[5], in_1[5]);
  and and_7 (out_3[6], in_2[6], in_1[6]);
  and and_8 (out_3[7], in_2[7], in_1[7]);
  and and_9 (out_3[8], in_1[8], in_2[8]);
  and and_10 (out_3[9], in_1[9], in_2[9]);
  and and_11 (out_3[10], in_1[10], in_2[10]);
  and and_12 (out_3[11], in_1[11], in_2[11]);
  and and_13 (out_3[12], in_1[12], in_2[12]);
  and and_14 (out_3[13], in_1[13], in_2[13]);
  and and_15 (out_3[14], in_1[14], in_2[14]);
  and and_16 (out_3[15], in_1[15], in_2[15]);
endmodule

module Or16Bit (
  input  [15:0] in_1,
  input  [15:0] in_2,
  output [15:0] out_3
);

  or or_1 (out_3[0], in_1[0], in_2[0]);
  or or_2 (out_3[1], in_2[1], in_1[1]);
  or or_3 (out_3[2], in_2[2], in_1[2]);
  or or_4 (out_3[3], in_2[3], in_1[3]);
  or or_5 (out_3[4], in_2[4], in_1[4]);
  or or_6 (out_3[5], in_2[5], in_1[5]);
  or or_7 (out_3[6], in_2[6], in_1[6]);
  or or_8 (out_3[7], in_2[7], in_1[7]);
  or or_9 (out_3[8], in_1[8], in_2[8]);
  or or_10 (out_3[9], in_1[9], in_2[9]);
  or or_11 (out_3[10], in_1[10], in_2[10]);
  or or_12 (out_3[11], in_1[11], in_2[11]);
  or or_13 (out_3[12], in_1[12], in_2[12]);
  or or_14 (out_3[13], in_1[13], in_2[13]);
  or or_15 (out_3[14], in_1[14], in_2[14]);
  or or_16 (out_3[15], in_1[15], in_2[15]);
endmodule

module XORGATE (
  input  in_1,
  input  in_2,
  output out_3
);

  wire and_1_out, not_1_out, or_1_out;

  and and_1 (and_1_out, in_1, in_2);
  not not_1 (not_1_out, and_1_out);
  or or_1 (or_1_out, in_1, in_2);
  and and_2 (out_3, not_1_out, or_1_out);
endmodule

module XOR16Bit (
  input  [15:0] in_1,
  input  [15:0] in_2,
  output [15:0] out_3
);

  XORGATE xorgate_1 (.in_1(in_1[0]), .in_2(in_2[0]), .out_3(out_3[0]));
  XORGATE xorgate_2 (.in_1(in_2[1]), .in_2(in_1[1]), .out_3(out_3[1]));
  XORGATE xorgate_3 (.in_1(in_2[2]), .in_2(in_1[2]), .out_3(out_3[2]));
  XORGATE xorgate_4 (.in_1(in_2[3]), .in_2(in_1[3]), .out_3(out_3[3]));
  XORGATE xorgate_5 (.in_1(in_2[4]), .in_2(in_1[4]), .out_3(out_3[4]));
  XORGATE xorgate_6 (.in_1(in_2[5]), .in_2(in_1[5]), .out_3(out_3[5]));
  XORGATE xorgate_7 (.in_1(in_2[6]), .in_2(in_1[6]), .out_3(out_3[6]));
  XORGATE xorgate_8 (.in_1(in_2[7]), .in_2(in_1[7]), .out_3(out_3[7]));
  XORGATE xorgate_9 (.in_1(in_1[8]), .in_2(in_2[8]), .out_3(out_3[8]));
  XORGATE xorgate_10 (.in_1(in_1[9]), .in_2(in_2[9]), .out_3(out_3[9]));
  XORGATE xorgate_11 (.in_1(in_1[10]), .in_2(in_2[10]), .out_3(out_3[10]));
  XORGATE xorgate_12 (.in_1(in_1[11]), .in_2(in_2[11]), .out_3(out_3[11]));
  XORGATE xorgate_13 (.in_1(in_1[12]), .in_2(in_2[12]), .out_3(out_3[12]));
  XORGATE xorgate_14 (.in_1(in_1[13]), .in_2(in_2[13]), .out_3(out_3[13]));
  XORGATE xorgate_15 (.in_1(in_1[14]), .in_2(in_2[14]), .out_3(out_3[14]));
  XORGATE xorgate_16 (.in_1(in_1[15]), .in_2(in_2[15]), .out_3(out_3[15]));
endmodule

module Check0 (
  input  [15:0] in_1,
  output out_2
);

  wire or_1_out, or_2_out, or_3_out, or_4_out, or_5_out, or_6_out, or_7_out, or_8_out, or_9_out, or_10_out,
       or_11_out, or_12_out, or_13_out, or_14_out;

  or or_1 (or_1_out, in_1[0], in_1[1]);
  or or_2 (or_2_out, in_1[2], in_1[3]);
  or or_3 (or_3_out, in_1[4], in_1[5]);
  or or_4 (or_4_out, in_1[6], in_1[7]);
  or or_5 (or_5_out, in_1[8], in_1[9]);
  or or_6 (or_6_out, in_1[10], in_1[11]);
  or or_7 (or_7_out, in_1[12], in_1[13]);
  or or_8 (or_8_out, in_1[14], in_1[15]);
  or or_9 (or_9_out, or_1_out, or_2_out);
  or or_10 (or_10_out, or_3_out, or_4_out);
  or or_11 (or_11_out, or_5_out, or_6_out);
  or or_12 (or_12_out, or_7_out, or_8_out);
  or or_13 (or_13_out, or_9_out, or_10_out);
  or or_14 (or_14_out, or_11_out, or_12_out);
  or or_15 (out_2, or_13_out, or_14_out);
endmodule

module ALU (
  input  [15:0] X,
  input  [15:0] Y,
  input  [5:0] ControlBits,
  output [15:0] O,
  output ng,
  output zr
);

  wire [15:0] and16bit_1_out_3, and16bit_2_out_3, and16bit_3_out_3, and16bit_4_out_3, and16bit_5_out_3,
       bitadder16_1_s, bitadder16_2_s, not16bit_1_out_2, xor16bit_1_out_3, xor16bit_2_out_3;
  wire [15:15] not_1_out, not_2_out, not_3_out;

  not not_1 (not_1_out[15], ControlBits[3]);
  not not_2 (not_2_out[15], ControlBits[5]);
  And16BIt and16bit_1 (.in_1(X), .in_2({16{not_2_out[15]}}), .out_3(and16bit_1_out_3));
  And16BIt and16bit_2 (.in_1({16{not_1_out[15]}}), .in_2(Y), .out_3(and16bit_2_out_3));
  XOR16Bit xor16bit_1 (.in_1(and16bit_1_out_3), .in_2({16{ControlBits[4]}}), .out_3(xor16bit_1_out_3));
  not not_3 (not_3_out[15], ControlBits[1]);
  XOR16Bit xor16bit_2 (.in_1({16{ControlBits[2]}}), .in_2(and16bit_2_out_3), .out_3(xor16bit_2_out_3));
  And16BIt and16bit_3 (.in_1(xor16bit_1_out_3), .in_2(xor16bit_2_out_3), .out_3(and16bit_3_out_3));
  And16BIt and16bit_4 (.in_1(and16bit_3_out_3), .in_2({16{not_3_out[15]}}), .out_3(and16bit_4_out_3));
  And16BIt and16bit_5 (.in_1(bitadder16_1_s), .in_2(not16bit_1_out_2), .out_3(and16bit_5_out_3));
  Not16Bit not16bit_1 (.in_1({16{not_3_out[15]}}), .out_2(not16bit_1_out_2));
  BitAdder16 bitadder16_1 (.A(xor16bit_2_out_3), .B(xor16bit_1_out_3), .S(bitadder16_1_s));
  BitAdder16 bitadder16_2 (.A(and16bit_4_out_3), .B(and16bit_5_out_3), .S(bitadder16_2_s));
  XOR16Bit xor16bit_3 (.in_1({16{ControlBits[0]}}), .in_2(bitadder16_2_s), .out_3({ng, O[14:0]}));
  Check0 check0_1 (.in_1({ng, O[14:0]}), .out_2(zr));

  assign O[15] = ng;
endmodule
